# Fritzing sketch RGBStrip (saved by Fritzing 0.9.2b)
circuit board: 6.88566cm x 5.36311cm
breadboards: 1

parts:
  R1 = Resistor [tolerance=±5% resistance=10k package=THT]
  R2 = Resistor [tolerance=±5% resistance=150 package=THT]
  R3 = Resistor [tolerance=±5% resistance=10k package=THT]
  R6 = Resistor [tolerance=±5% resistance=150 package=THT]
  R4 = Resistor [tolerance=±5% resistance=10k package=THT]
  R5 = Resistor [tolerance=±5% resistance=150 package=THT]
  Q1 = Basic FET N-Channel [package="TO220 [THT]"]
  Q2 = Basic FET N-Channel [package="TO220 [THT]"]
  Q3 = Basic FET N-Channel [package="TO220 [THT]"]
  JP2 = Header 2 [package=springterminal-2.54mm-2]
  JP3 = Header 2 [package=springterminal-2.54mm-2]
  Q4 = Basic FET N-Channel [package="TO220 [THT]"]
  Q5 = Basic FET N-Channel [package="TO220 [THT]"]
  Q6 = Basic FET N-Channel [package="TO220 [THT]"]
  R7 = Resistor [tolerance=±5% resistance=10k package=THT]
  R8 = Resistor [tolerance=±5% resistance=10k package=THT]
  R9 = Resistor [tolerance=±5% resistance=10k package=THT]
  R10 = Resistor [tolerance=±5% resistance=150 package=THT]
  R11 = Resistor [tolerance=±5% resistance=150 package=THT]
  R12 = Resistor [tolerance=±5% resistance=150 package=THT]
  Part1 = Arduino Uno (Rev3)
  JP4 = Header 2 [package=springterminal-2.54mm-2]
  JP5 = Header 2 [package=springterminal-2.54mm-2]

nets:
  N1: R1.Pin_0, R2.Pin_0, Q1.gate
  N2: R1.Pin_1, R3.Pin_1, R4.Pin_1, Q1.source, Q2.source, Q3.source, JP3.1, Q4.source, Q5.source, Q6.source, R7.Pin_1, R8.Pin_1, R9.Pin_1, Part1.GND, JP4.2
  N3: R2.Pin_1, Part1.D11_PWM/MOSI
  N4: R3.Pin_0, R5.Pin_0, Q2.gate
  N5: R6.Pin_0, R4.Pin_0, Q3.gate
  N6: R6.Pin_1, Part1.D9_PWM
  N7: R5.Pin_1, Part1.D10_PWM/SS
  N8: Q1.drain, JP4.1
  N9: Q2.drain, JP5.2
  N10: Q3.drain, JP5.1
  N11: JP2.1, Q5.drain
  N12: JP2.2, Q6.drain
  N13: JP3.2, Q4.drain
  N14: Q4.gate, R7.Pin_0, R10.Pin_0
  N15: Q5.gate, R8.Pin_0, R11.Pin_0
  N16: Q6.gate, R9.Pin_0, R12.Pin_0
  N17: R10.Pin_1, Part1.D6_PWM
  N18: R11.Pin_1, Part1.D5_PWM
  N19: R12.Pin_1, Part1.D3_PWM
